// Logisim project mycpu.circ as structural Verilog
module main (
  input  reset,
  output [31:0] instruction,
  output RegWrite,
  output [4:0] RegAddr,
  output [31:0] RegData,
  output MemWrite,
  output [4:0] MemAddr,
  output [31:0] MemData
);

  wire ALUSrc, Clk, extendType, MemRead, ZERO;
  wire [1:0] MemotoReg, RegDst;
  wire [2:0] DMtype, PCControl;
  wire [3:0] ALUControl;
  wire [4:0] rd, rs, rt, shift;
  wire [5:0] Function, Opcode;
  wire [15:0] immed;
  wire [25:0] Jimme;
  wire [31:0] A, ALUout, B, bit_extender_1_out, bit_extender_2_out, immedExtend, Lwdata, multiplexer_4_out,
       olddata, PC, PC4, PCNext;

  Clock clock_1 (.out(Clk));
  Register #(.width(32)) u_PC (.D(PCNext), .Q(PC), .clk(Clk));  // open: en, clr
  assign bit_extender_1_out = {{16{1'b0}}, immed};  // Bit_Extender bit_extender_1
  assign bit_extender_2_out = {{16{immed[15]}}, immed};  // Bit_Extender bit_extender_2
  IM im_1 (.in_1(PC), .out_2(instruction));
  Multiplexer #(.select(2), .width(5), .enable("false")) multiplexer_1 (
    .in0(rt), .in1(rd), .in2({5{1'b1}}), .out(RegAddr), .sel(RegDst));  // open: in3
  getPC getpc_1 (
    .PC(PC), .immed(immed), .Jimme(Jimme), .reset(reset), .RA(A), .PCControl(PCControl), .PCNext(PCNext),
    .PC4(PC4));
  Multiplexer #(.select(2), .width(32), .enable("false")) multiplexer_2 (
    .in0({ALUout[31:7], MemAddr, ALUout[1:0]}), .in1(Lwdata), .in2(PC4), .out(RegData), .sel(MemotoReg));  // open: in3
  Multiplexer #(.width(32), .enable("false")) multiplexer_3 (
    .in0(bit_extender_1_out), .in1(bit_extender_2_out), .out(immedExtend), .sel(extendType));
  Control control_1 (
    .Opcode(Opcode), .Function(Function), .Zero(ZERO), .ALUControl(ALUControl), .RegDst(RegDst),
    .RegWrite(RegWrite), .ALUSrc(ALUSrc), .MemWrite(MemWrite), .MemtoReg(MemotoReg), .MemRead(MemRead),
    .PCControl(PCControl), .extendType(extendType), .DMtype(DMtype));
  SplitInstruction splitinstruction_1 (
    .Instruction(instruction), .immed(immed), .Function(Function), .shift(shift), .Rd(rd), .Rt(rt), .Rs(rs),
    .Op(Opcode), .Jimme(Jimme));
  getDM getdm_1 (
    .in_4(DMtype), .address({ALUout[31:7], MemAddr, ALUout[1:0]}), .rtData(B), .olddata(olddata),
    .DMout(MemData));
  grf grf_1 (.A1(rs), .A2(rt), .A3(RegAddr), .WD(RegData), .clk(Clk), .reset(reset), .we(RegWrite), .RD1(A), .RD2(B));
  Multiplexer #(.width(32), .enable("false")) multiplexer_4 (
    .in0(B), .in1(immedExtend), .out(multiplexer_4_out), .sel(ALUSrc));
  ALU alu_1 (
    .A(A), .B(multiplexer_4_out), .ALUOP(ALUControl), .ZERO(ZERO),
    .Out({ALUout[31:7], MemAddr, ALUout[1:0]}), .shmnt(shift));
  DM dm_1 (
    .Address({ALUout[31:7], MemAddr, ALUout[1:0]}), .Data(MemData), .MemWrite(MemWrite), .MemRead(MemRead),
    .clock(Clk), .reset(reset), .Output(olddata));
  getDMout getdmout_1 (.data(olddata), .addr({ALUout[31:7], MemAddr, ALUout[1:0]}), .\type (DMtype), .out_4(Lwdata));

  // Other names for the same wires on the sheet: DMin[31:0] = MemData;
  //   MemAddr_t[31:0] = {ALUout[31:7], MemAddr, ALUout[1:0]}; ALUout[6:2] = MemAddr; WD[31:0] = RegData
endmodule

// isSw
module Control (
  input  [5:0] Opcode,
  input  [5:0] Function,
  input  Zero,
  output [3:0] ALUControl,
  output [1:0] RegDst,
  output RegWrite,
  output ALUSrc,
  output MemWrite,
  output [1:0] MemtoReg,
  output MemRead,
  output [2:0] PCControl,
  output extendType,
  output [2:0] DMtype
);

  wire addi, addu, \and , and_9_out, beq, branch, comparator_1_eq, comparator_2_eq, comparator_3_eq,
       comparator_4_eq, comparator_5_eq, comparator_6_eq, comparator_7_eq, comparator_8_eq, J, jal, jr, lh,
       lhu, lui, lw, \or , or_1_out, or_2_out, or_6_out, or_7_out, or_9_out, or_10_out, or_11_out, or_12_out,
       or_13_out, ori, R, sh, sll, sllv, slt, slti, subu, sw;

  Comparator #(.width(6)) comparator_1 (.a(Function), .b(6'b100001), .eq(comparator_1_eq));  // open: gt, lt
  and and_1 (addu, comparator_1_eq, R);
  Comparator #(.width(6)) comparator_2 (.a(Function), .b(6'b100011), .eq(comparator_2_eq));  // open: gt, lt
  and and_2 (subu, comparator_2_eq, R);
  Comparator #(.width(6)) comparator_3 (.a(Function), .b(6'b100100), .eq(comparator_3_eq));  // open: gt, lt
  and and_3 (\and , comparator_3_eq, R);
  Comparator #(.width(6)) comparator_4 (.a(Function), .b(6'b100111), .eq(comparator_4_eq));  // open: gt, lt
  and and_4 (\or , comparator_4_eq, R);
  Comparator #(.width(6)) comparator_5 (.a(Function), .b({6{1'b0}}), .eq(comparator_5_eq));  // open: gt, lt
  and and_5 (sll, comparator_5_eq, R);
  Comparator #(.width(6)) comparator_6 (.a(Function), .b(6'b000100), .eq(comparator_6_eq));  // open: gt, lt
  and and_6 (sllv, comparator_6_eq, R);
  Comparator #(.width(6)) comparator_7 (.a(Function), .b(6'b101010), .eq(comparator_7_eq));  // open: gt, lt
  and and_7 (slt, comparator_7_eq, R);
  Comparator #(.width(6)) comparator_8 (.a(Function), .b(6'b001000), .eq(comparator_8_eq));  // open: gt, lt
  and and_8 (jr, comparator_8_eq, R);
  Comparator #(.width(6), .mode("unsigned")) comparator_9 (.a(Opcode), .b({6{1'b0}}), .eq(R));  // open: gt, lt
  Comparator #(.width(6)) comparator_10 (.a(Opcode), .b(6'b001000), .eq(addi));  // open: gt, lt
  Comparator #(.width(6)) comparator_11 (.a(Opcode), .b(6'b001101), .eq(ori));  // open: gt, lt
  Comparator #(.width(6)) comparator_12 (.a(Opcode), .b(6'b001111), .eq(lui));  // open: gt, lt
  Comparator #(.width(6)) comparator_13 (.a(Opcode), .b(6'b001010), .eq(slti));  // open: gt, lt
  buf or_1 (or_1_out, jal);  // OR_Gate
  buf or_2 (or_2_out, jal);  // OR_Gate
  and and_9 (and_9_out, beq, Zero);
  or or_3 (MemRead, lw, lh, lhu);
  or or_4 (MemWrite, sw, sh);
  buf or_5 (branch, beq);  // OR_Gate
  or or_6 (or_6_out, lw, sw);
  or or_7 (or_7_out, lh, sh);
  Priority_Encoder #(.select(2)) priority_encoder_1 (
    .in1(R), .in2(or_1_out), .out(RegDst));  // open: in0, in3, gs, en_out, en_in
  Priority_Encoder #(.select(2)) priority_encoder_2 (
    .in1(MemRead), .in2(or_2_out), .out(MemtoReg));  // open: in0, in3, gs, en_out, en_in
  or or_8 (extendType, MemWrite, addi, MemRead);
  Comparator #(.width(6)) comparator_14 (.a(Opcode), .b(6'b000100), .eq(beq));  // open: gt, lt
  buf or_9 (or_9_out, sll);  // OR_Gate
  or or_10 (or_10_out, slt, slti);
  Pull_Resistor pull_resistor_1 (.node(RegDst));
  nor nor_1 (RegWrite, MemWrite, branch, J, jr);
  nor nor_2 (ALUSrc, R, branch, J, jal);
  Pull_Resistor pull_resistor_2 (.node(MemtoReg));
  Priority_Encoder priority_encoder_3 (
    .in1(and_9_out), .in2(J), .in3(jal), .in4(jr), .out(PCControl));  // open: in0, in5, in6, in7, en_in, gs, en_out
  Pull_Resistor pull_resistor_3 (.node(DMtype));
  Priority_Encoder priority_encoder_4 (
    .in0(or_6_out), .in1(or_7_out), .in2(lhu), .out(DMtype));  // open: in3, in4, in5, in6, in7, en_in, gs, en_out
  or or_11 (or_11_out, subu, beq);
  buf or_12 (or_12_out, \and );  // OR_Gate
  buf or_13 (or_13_out, ori);  // OR_Gate
  Pull_Resistor pull_resistor_4 (.node(PCControl));
  Comparator #(.width(6)) comparator_15 (.a(Opcode), .b(6'b000010), .eq(J));  // open: gt, lt
  Comparator #(.width(6)) comparator_16 (.a(Opcode), .b(6'b000011), .eq(jal));  // open: gt, lt
  Priority_Encoder #(.select(4)) priority_encoder_5 (
    .in1(or_11_out), .in2(or_12_out), .in3(or_13_out), .in4(or_9_out), .in5(or_10_out), .in6(lui),
    .in7(sllv), .out(ALUControl));  // open: in0, in8, in9, in10, in11, in12, in13, in14, in15, gs, en_out, en_in
  Pull_Resistor pull_resistor_5 (.node(ALUControl));
  Comparator #(.width(6)) comparator_17 (.a(Opcode), .b(6'b101011), .eq(sw));  // open: gt, lt
  Comparator #(.width(6)) comparator_18 (.a(Opcode), .b(6'b101001), .eq(sh));  // open: gt, lt
  Comparator #(.width(6)) comparator_19 (.a(Opcode), .b(6'b100011), .eq(lw));  // open: gt, lt
  Comparator #(.width(6)) comparator_20 (.a(Opcode), .b(6'b100001), .eq(lh));  // open: gt, lt
  Comparator #(.width(6)) comparator_21 (.a(Opcode), .b(6'b100101), .eq(lhu));  // open: gt, lt

  // Other names for the same wires on the sheet: func[5:0] = Function; load = MemRead; store = MemWrite

  // Notes on the sheet:
  //   符号扩展的指令
  //   存储器位长类型
endmodule

module ALU (
  input  [31:0] A,
  input  [4:0] shmnt,
  input  [31:0] B,
  input  [3:0] ALUOP,
  output ZERO,
  output [31:0] Out
);

  wire comparator_1_lt;
  wire [31:0] ADD, \and , lui, OR, shift, sllv, slt, SUB;

  Adder #(.width(32)) adder_1 (.a(A), .b(B), .out(ADD));  // open: cin, cout
  Subtractor #(.width(32)) subtractor_1 (.a(A), .b(B), .out(SUB));  // open: bin, bout
  assign OR = A | B;  // OR_Gate or_1, 32 bits wide
  assign \and  = A & B;  // AND_Gate and_1, 32 bits wide
  Shifter #(.width(32)) shifter_1 (.in(B), .\dist (shmnt), .out(shift));
  Comparator #(.width(32), .mode("unsigned")) comparator_1 (.a(A), .b(B), .lt(comparator_1_lt));  // open: gt, eq
  assign slt = {{31{1'b0}}, comparator_1_lt};  // Bit_Extender bit_extender_1
  Shifter #(.width(32)) shifter_2 (.in(B), .\dist (5'b10000), .out(lui));
  Shifter #(.width(32)) shifter_3 (.in(B), .\dist (A[4:0]), .out(sllv));
  Comparator #(.width(32), .mode("unsigned")) comparator_2 (.a(SUB), .b({32{1'b0}}), .eq(ZERO));  // open: gt, lt
  Multiplexer #(.select(4), .width(32), .enable("false")) multiplexer_1 (
    .in0(ADD), .in1(SUB), .in2(\and ), .in3(OR), .in4(shift), .in5(slt), .in6(lui), .in7(sllv), .out(Out),
    .sel(ALUOP));  // open: in8, in9, in10, in11, in12, in13, in14, in15
endmodule

module SplitInstruction (
  input  [31:0] Instruction,
  output [15:0] immed,
  output [5:0] Function,
  output [4:0] shift,
  output [4:0] Rd,
  output [4:0] Rt,
  output [4:0] Rs,
  output [5:0] Op,
  output [25:0] Jimme
);


  assign Function = Instruction[5:0];
  assign immed = Instruction[15:0];
  assign Jimme = Instruction[25:0];
  assign Op = Instruction[31:26];
  assign Rd = Instruction[15:11];
  assign Rs = Instruction[25:21];
  assign Rt = Instruction[20:16];
  assign shift = Instruction[10:6];
endmodule

module IM (
  input  [31:0] in_1,
  output [31:0] out_2
);

  ROM #(.addrWidth(5), .dataWidth(32)) rom_1 (.addr(in_1[6:2]), .data(out_2));  // open: sel
endmodule

module DM (
  input  reset,
  input  [31:0] Address,
  input  [31:0] Data,
  input  MemWrite,
  input  MemRead,
  input  clock,
  output [31:0] Output
);

  RAM #(.addrWidth(5), .dataWidth(32), .bus("separate")) ram_1 (
    .addr(Address[6:2]), .din(Data), .data(Output), .str(MemWrite), .clk(clock), .ld(MemRead), .clr(reset));  // open: sel
endmodule

module getPC (
  input  reset,
  input  [31:0] PC,
  input  [15:0] immed,
  input  [25:0] Jimme,
  input  [2:0] PCControl,
  input  [31:0] RA,
  output [31:0] PCNext,
  output [31:0] PC4
);

  wire [31:0] bit_extender_1_out, Branchpc, multiplexer_1_out, shifter_1_out;

  assign bit_extender_1_out = {{16{immed[15]}}, immed};  // Bit_Extender bit_extender_1
  Adder #(.width(32)) adder_1 (.a(PC), .b(32'h4), .out(PC4));  // open: cin, cout
  Shifter #(.width(32)) shifter_1 (.in(bit_extender_1_out), .\dist (5'b00010), .out(shifter_1_out));
  Multiplexer #(.select(3), .width(32), .enable("false")) multiplexer_1 (
    .in0(PC4), .in1(Branchpc), .in2({PC4[31:28], Jimme, 2'b00}), .in3({PC4[31:28], Jimme, 2'b00}), .in4(RA),
    .out(multiplexer_1_out), .sel(PCControl));  // open: in5, in6, in7
  Adder #(.width(32)) adder_2 (.a(shifter_1_out), .b(PC4), .out(Branchpc));  // open: cin, cout
  Multiplexer #(.width(32), .enable("false")) multiplexer_2 (
    .in0(multiplexer_1_out), .in1(32'h3000), .out(PCNext), .sel(reset));

  // Other names for the same wires on the sheet: Jpc[31:2] = {PC4[31:28], Jimme}
endmodule

module grf (
  input  [4:0] A1,
  input  clk,
  input  reset,
  input  we,
  input  [4:0] A2,
  input  [4:0] A3,
  input  [31:0] WD,
  output [31:0] RD1,
  output [31:0] RD2
);

  wire [31:0] I0, I1, I2, I3, I4, I5, I6, I7, I8, I9, I10, I11, I12, I13, I14, I15, I16, I17, I18, I19, I20,
       I21, I22, I23, I24, I25, I26, I27, I28, I29, I30, I31, O0, O1, O2, O3, O4, O5, O6, O7, O8, O9, O10,
       O11, O12, O13, O14, O15, O16, O17, O18, O19, O20, O21, O22, O23, O24, O25, O26, O27, O28, O29, O30,
       O31;

  Demultiplexer #(.select(5), .width(32), .tristate("true")) demultiplexer_1 (
    .out0(I0), .out1(I1), .out2(I2), .out3(I3), .out4(I4), .out5(I5), .out6(I6), .out7(I7), .out8(I8),
    .out9(I9), .out10(I10), .out11(I11), .out12(I12), .out13(I13), .out14(I14), .out15(I15), .out16(I16),
    .out17(I17), .out18(I18), .out19(I19), .out20(I20), .out21(I21), .out22(I22), .out23(I23), .out24(I24),
    .out25(I25), .out26(I26), .out27(I27), .out28(I28), .out29(I29), .out30(I30), .out31(I31), .in(WD),
    .sel(A3));  // open: en
  Multiplexer #(.select(5), .width(32)) multiplexer_1 (
    .in0(O0), .in1(O1), .in2(O2), .in3(O3), .in4(O4), .in5(O5), .in6(O6), .in7(O7), .in8(O8), .in9(O9),
    .in10(O10), .in11(O11), .in12(O12), .in13(O13), .in14(O14), .in15(O15), .in16(O16), .in17(O17),
    .in18(O18), .in19(O19), .in20(O20), .in21(O21), .in22(O22), .in23(O23), .in24(O24), .in25(O25),
    .in26(O26), .in27(O27), .in28(O28), .in29(O29), .in30(O30), .in31(O31), .out(RD2), .sel(A2));  // open: en
  Multiplexer #(.select(5), .width(32)) multiplexer_2 (
    .in0(O0), .in1(O1), .in2(O2), .in3(O3), .in4(O4), .in5(O5), .in6(O6), .in7(O7), .in8(O8), .in9(O9),
    .in10(O10), .in11(O11), .in12(O12), .in13(O13), .in14(O14), .in15(O15), .in16(O16), .in17(O17),
    .in18(O18), .in19(O19), .in20(O20), .in21(O21), .in22(O22), .in23(O23), .in24(O24), .in25(O25),
    .in26(O26), .in27(O27), .in28(O28), .in29(O29), .in30(O30), .in31(O31), .out(RD1), .sel(A1));  // open: en
  Register #(.width(32)) register_1 (.D({32{1'b0}}), .en(we), .Q(O0), .clk(clk), .clr(reset));
  Register #(.width(32)) register_2 (.D(I8), .en(we), .Q(O8), .clk(clk), .clr(reset));
  Register #(.width(32)) register_3 (.D(I16), .en(we), .Q(O16), .clk(clk), .clr(reset));
  Register #(.width(32)) register_4 (.D(I24), .en(we), .Q(O24), .clk(clk), .clr(reset));
  Register #(.width(32)) register_5 (.D(I1), .en(we), .Q(O1), .clk(clk), .clr(reset));
  Register #(.width(32)) register_6 (.D(I9), .en(we), .Q(O9), .clk(clk), .clr(reset));
  Register #(.width(32)) register_7 (.D(I17), .en(we), .Q(O17), .clk(clk), .clr(reset));
  Register #(.width(32)) register_8 (.D(I25), .en(we), .Q(O25), .clk(clk), .clr(reset));
  Register #(.width(32)) register_9 (.D(I2), .en(we), .Q(O2), .clk(clk), .clr(reset));
  Register #(.width(32)) register_10 (.D(I10), .en(we), .Q(O10), .clk(clk), .clr(reset));
  Register #(.width(32)) register_11 (.D(I18), .en(we), .Q(O18), .clk(clk), .clr(reset));
  Register #(.width(32)) register_12 (.D(I26), .en(we), .Q(O26), .clk(clk), .clr(reset));
  Register #(.width(32)) register_13 (.D(I3), .en(we), .Q(O3), .clk(clk), .clr(reset));
  Register #(.width(32)) register_14 (.D(I11), .en(we), .Q(O11), .clk(clk), .clr(reset));
  Register #(.width(32)) register_15 (.D(I19), .en(we), .Q(O19), .clk(clk), .clr(reset));
  Register #(.width(32)) register_16 (.D(I27), .en(we), .Q(O27), .clk(clk), .clr(reset));
  Register #(.width(32)) register_17 (.D(I4), .en(we), .Q(O4), .clk(clk), .clr(reset));
  Register #(.width(32)) register_18 (.D(I12), .en(we), .Q(O12), .clk(clk), .clr(reset));
  Register #(.width(32)) register_19 (.D(I20), .en(we), .Q(O20), .clk(clk), .clr(reset));
  Register #(.width(32)) register_20 (.D(I28), .en(we), .Q(O28), .clk(clk), .clr(reset));
  Register #(.width(32)) register_21 (.D(I5), .en(we), .Q(O5), .clk(clk), .clr(reset));
  Register #(.width(32)) register_22 (.D(I13), .en(we), .Q(O13), .clk(clk), .clr(reset));
  Register #(.width(32)) register_23 (.D(I21), .en(we), .Q(O21), .clk(clk), .clr(reset));
  Register #(.width(32)) register_24 (.D(I29), .en(we), .Q(O29), .clk(clk), .clr(reset));
  Register #(.width(32)) register_25 (.D(I6), .en(we), .Q(O6), .clk(clk), .clr(reset));
  Register #(.width(32)) register_26 (.D(I14), .en(we), .Q(O14), .clk(clk), .clr(reset));
  Register #(.width(32)) register_27 (.D(I22), .en(we), .Q(O22), .clk(clk), .clr(reset));
  Register #(.width(32)) register_28 (.D(I30), .en(we), .Q(O30), .clk(clk), .clr(reset));
  Register #(.width(32)) register_29 (.D(I7), .en(we), .Q(O7), .clk(clk), .clr(reset));
  Register #(.width(32)) register_30 (.D(I15), .en(we), .Q(O15), .clk(clk), .clr(reset));
  Register #(.width(32)) register_31 (.D(I23), .en(we), .Q(O23), .clk(clk), .clr(reset));
  Register #(.width(32)) register_32 (.D(I31), .en(we), .Q(O31), .clk(clk), .clr(reset));
endmodule

module getDM (
  input  [31:0] address,
  input  [31:0] rtData,
  input  [31:0] olddata,
  input  [2:0] in_4,
  output [31:0] DMout
);

  wire [15:0] multiplexer_1_out;
  wire [31:0] bit_extender_1_out, bit_extender_2_out, or_1_out, or_2_out, sh, shifter_1_out, shifter_2_out;

  Multiplexer #(.width(16), .enable("false")) multiplexer_1 (
    .in0(olddata[31:16]), .in1(olddata[15:0]), .out(multiplexer_1_out), .sel(address[1]));
  assign bit_extender_1_out = {{16{1'b0}}, multiplexer_1_out};  // Bit_Extender bit_extender_1
  assign bit_extender_2_out = {{16{1'b0}}, rtData[15:0]};  // Bit_Extender bit_extender_2
  Shifter #(.width(32)) shifter_1 (.in(bit_extender_1_out), .\dist (5'b10000), .out(shifter_1_out));
  Shifter #(.width(32)) shifter_2 (.in(bit_extender_2_out), .\dist (5'b10000), .out(shifter_2_out));
  assign or_1_out = shifter_1_out | bit_extender_2_out;  // OR_Gate or_1, 32 bits wide
  assign or_2_out = bit_extender_1_out | shifter_2_out;  // OR_Gate or_2, 32 bits wide
  Multiplexer #(.select(3), .width(32)) multiplexer_2 (
    .in0(rtData), .in1(sh), .out(DMout), .sel(in_4));  // open: in2, in3, in4, in5, in6, in7, en
  Multiplexer #(.width(32), .enable("false")) multiplexer_3 (
    .in0(or_1_out), .in1(or_2_out), .out(sh), .sel(address[1]));

  // Other names for the same wires on the sheet: sw[31:0] = rtData; type[2:0] = in_4
endmodule

module getDMout (
  input  [31:0] addr,
  input  [2:0] \type ,
  input  [31:0] data,
  output [31:0] out_4
);

  wire [15:0] multiplexer_1_out, multiplexer_2_out;
  wire [31:0] lh, lhu;

  Multiplexer #(.width(16)) multiplexer_1 (
    .in0(data[15:0]), .in1(data[31:16]), .out(multiplexer_1_out), .sel(addr[1]));  // open: en
  assign lh = {{16{multiplexer_1_out[15]}}, multiplexer_1_out};  // Bit_Extender bit_extender_1
  Multiplexer #(.width(16)) multiplexer_2 (
    .in0(data[15:0]), .in1(data[31:16]), .out(multiplexer_2_out), .sel(addr[1]));  // open: en
  assign lhu = {{16{1'b0}}, multiplexer_2_out};  // Bit_Extender bit_extender_2
  Multiplexer #(.select(3), .width(32)) multiplexer_3 (
    .in0(data), .in1(lh), .in2(lhu), .out(out_4), .sel(\type ));  // open: in3, in4, in5, in6, in7, en

  // Other names for the same wires on the sheet: lw[31:0] = data
endmodule
